# Fritzing sketch Plot Clock (saved by Fritzing 0.9.3b)

parts:
  Part1 = Arduino Uno (Rev3) - ICSP
  LED1 = LEDs [package=led10mm]
  J1 = Basic Servo
  Part2 = KY-012
  J2 = Basic Servo
  PIR1 = PIR sensor
  Part3 = Breakout Board for Electret Microphone
  Part5 = Adafruit DS1307 RTC Breakout [part_number="Adafruit #264"]

nets:
  N1: Part1.A4/SDA, Part5.SDA
  N2: Part1.A5/SCL, Part5.SCL
  N3: Part1.D13/SCK, Part3.AUD
  GND: Part1.GND, LED1.A, Part2.connector0, PIR1.GND, Part3.GND, Part5.GND
  N4: Part1.D4, PIR1.SIG
  N5: Part1.D5_PWM, J2.pulse
  N6: Part1.D6_PWM, J1.pulse
  N7: Part1.D7, LED1.C
  VCC: Part1.5V, J1.vcc, Part2.connector2, J2.vcc, PIR1.VDD, Part3.VCC, Part5.VCC

custom parts:
  Adafruit DS1307 RTC Breakout: This is a great battery-backed real time clock (RTC) that allows your microcontroller project to keep track of time even if it is reprogrammed, or if the power is lost. Perfect for datalogging, clock-building, time stamping, timers and alarms, etc. The DS1307 is the most popular RTC - but it requires 5V power to work (although we've used it with 5V power and 3.3V logic successfully) PCB &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
